// Logisim project logic.circ as structural Verilog: 9 circuits, main circuit main
module main (
  input  [4:0] in_1,
  input  [7:0] in_2,
  input  [7:0] in_3,
  input  [7:0] in_4,
  input  [7:0] in_5,
  input  [7:0] in_6,
  input  [7:0] in_7,
  input  [7:0] in_8,
  input  [7:0] in_9,
  input  [7:0] in_10,
  input  [7:0] in_11,
  input  [7:0] in_12,
  input  [7:0] in_13,
  input  [7:0] in_14,
  input  [7:0] in_15,
  input  [7:0] in_16,
  input  [7:0] in_17,
  input  [7:0] in_18,
  input  [7:0] in_19,
  input  [7:0] in_20,
  input  [7:0] in_21,
  input  [7:0] in_22,
  input  [7:0] in_23,
  input  [7:0] in_24,
  input  [7:0] in_25,
  input  [7:0] in_26,
  input  [7:0] in_27,
  input  [7:0] in_28,
  input  [7:0] in_29,
  input  [7:0] in_30,
  input  [7:0] in_31,
  input  [7:0] in_32,
  input  [7:0] in_33,
  input  [31:0] in_34,
  input  [4:0] in_35,
  input  in_36,
  input  [3:0] in_37,
  input  [3:0] in_38,
  input  [2:0] in_39,
  output out_40,
  output [7:0] out_41,
  output out_42,
  output [7:0] out_43,
  output OUT0,
  output OUT1,
  output OUT2,
  output OUT3,
  output OUT4,
  output OUT5,
  output OUT6,
  output OUT7,
  output [2:0] out_52,
  output OUT8,
  output [2:0] out_54,
  output OUT9,
  output [2:0] out_56,
  output OUT10,
  output [2:0] out_58,
  output OUT11,
  output [2:0] out_60,
  output OUT12,
  output [2:0] out_62,
  output OUT13,
  output [2:0] out_64,
  output OUT14,
  output [2:0] out_66,
  output OUT15,
  output [2:0] out_68,
  output [2:0] out_69,
  output [2:0] out_70,
  output [2:0] out_71,
  output out_72,
  output out_73,
  output [2:0] out_74,
  output out_75,
  output out_76,
  output [2:0] out_77,
  output out_78,
  output out_79,
  output [2:0] out_80,
  output out_81,
  output out_82,
  output [2:0] out_83,
  output out_84,
  output out_85,
  output out_86,
  output out_87,
  output out_88,
  output out_89,
  output out_90,
  output out_91,
  output [2:0] out_92,
  output [2:0] out_93,
  output [2:0] out_94,
  output [2:0] out_95,
  output [2:0] out_96,
  output [2:0] out_97,
  output [2:0] out_98,
  output [2:0] out_99,
  output [2:0] out_100,
  output [2:0] out_101,
  output [2:0] out_102,
  output [2:0] out_103,
  output [2:0] out_104,
  output [2:0] out_105,
  output [2:0] out_106,
  output [2:0] out_107
);

  Demultiplexer #(.select(4)) demultiplexer_1 (
    .out0(out_72), .out1(out_73), .out2(out_75), .out3(out_76), .out4(out_78), .out5(out_79), .out6(out_81),
    .out7(out_82), .out8(out_84), .out9(out_85), .out10(out_86), .out11(out_87), .out12(out_88),
    .out13(out_89), .out14(out_90), .out15(out_91), .in(in_36), .sel(in_37));
  DMX_1_16 dmx_1_16_1 (
    .en(in_36), .ADDR(in_37), .OUT0(OUT0), .OUT1(OUT1), .OUT2(OUT2), .OUT3(OUT3), .OUT4(OUT4), .OUT5(OUT5),
    .OUT6(OUT6), .OUT7(OUT7), .OUT8(OUT8), .OUT9(OUT9), .OUT10(OUT10), .OUT11(OUT11), .OUT12(OUT12),
    .OUT13(OUT13), .OUT14(OUT14), .OUT15(OUT15));
  Multiplexer #(.select(5)) multiplexer_1 (
    .in0(in_34[0]), .in1(in_34[1]), .in2(in_34[2]), .in3(in_34[3]), .in4(in_34[4]), .in5(in_34[5]),
    .in6(in_34[6]), .in7(in_34[7]), .in8(in_34[8]), .in9(in_34[9]), .in10(in_34[10]), .in11(in_34[11]),
    .in12(in_34[12]), .in13(in_34[13]), .in14(in_34[14]), .in15(in_34[15]), .in16(in_34[16]),
    .in17(in_34[17]), .in18(in_34[18]), .in19(in_34[19]), .in20(in_34[20]), .in21(in_34[21]),
    .in22(in_34[22]), .in23(in_34[23]), .in24(in_34[24]), .in25(in_34[25]), .in26(in_34[26]),
    .in27(in_34[27]), .in28(in_34[28]), .in29(in_34[29]), .in30(in_34[30]), .in31(in_34[31]), .out(out_42),
    .sel(in_35));
  MUX_32_5_Gate mux_32_5_gate_1 (
    .D0(in_34[0]), .D1(in_34[1]), .D2(in_34[2]), .D3(in_34[3]), .D4(in_34[4]), .D5(in_34[5]), .D6(in_34[6]),
    .D7(in_34[7]), .D8(in_34[8]), .D9(in_34[9]), .D10(in_34[10]), .D11(in_34[11]), .D12(in_34[12]),
    .control_bit(in_35), .D13(in_34[13]), .D14(in_34[14]), .D15(in_34[15]), .D16(in_34[16]), .D17(in_34[17]),
    .D18(in_34[18]), .D19(in_34[19]), .D20(in_34[20]), .D21(in_34[21]), .D22(in_34[22]), .D23(in_34[23]),
    .D24(in_34[24]), .D25(in_34[25]), .D26(in_34[26]), .D27(in_34[27]), .D28(in_34[28]), .D29(in_34[29]),
    .D30(in_34[30]), .D31(in_34[31]), .out_34(out_40));
  Demultiplexer #(.select(4), .width(3)) demultiplexer_2 (
    .out0(out_92), .out1(out_93), .out2(out_94), .out3(out_95), .out4(out_96), .out5(out_97), .out6(out_98),
    .out7(out_99), .out8(out_100), .out9(out_101), .out10(out_102), .out11(out_103), .out12(out_104),
    .out13(out_105), .out14(out_106), .out15(out_107), .in(in_39), .sel(in_38));
  DMX_7bit dmx_7bit_1 (
    .ADDR(in_38), .EN(in_39), .out_3(out_52), .out_4(out_54), .out_5(out_56), .out_6(out_58), .out_7(out_60),
    .out_8(out_62), .out_9(out_64), .out_10(out_66), .out_11(out_68), .out_12(out_69), .out_13(out_70),
    .out_14(out_71), .out_15(out_74), .out_16(out_77), .out_17(out_80), .out_18(out_83));
  Multiplexer #(.select(5), .width(8)) multiplexer_2 (
    .in0(in_2), .in1(in_3), .in2(in_4), .in3(in_5), .in4(in_6), .in5(in_7), .in6(in_8), .in7(in_9),
    .in8(in_10), .in9(in_11), .in10(in_12), .in11(in_13), .in12(in_14), .in13(in_15), .in14(in_16),
    .in15(in_17), .in16(in_18), .in17(in_19), .in18(in_20), .in19(in_21), .in20(in_22), .in21(in_23),
    .in22(in_24), .in23(in_25), .in24(in_26), .in25(in_27), .in26(in_28), .in27(in_29), .in28(in_30),
    .in29(in_31), .in30(in_32), .in31(in_33), .out(out_43), .sel(in_1));
  MUX_32_8_BIT mux_32_8_bit_1 (
    .ADDR(in_1), .in_2(in_2), .in_3(in_3), .in_4(in_4), .in_5(in_5), .in_6(in_6), .in_7(in_7), .in_8(in_8),
    .in_9(in_9), .in_10(in_10), .in_11(in_11), .in_12(in_12), .in_13(in_13), .in_14(in_14), .in_15(in_15),
    .in_16(in_16), .in_17(in_17), .in_18(in_18), .in_19(in_19), .in_20(in_20), .in_21(in_21), .in_22(in_22),
    .in_23(in_23), .in_24(in_24), .in_25(in_25), .in_26(in_26), .in_27(in_27), .in_28(in_28), .in_29(in_29),
    .in_30(in_30), .in_31(in_31), .in_32(in_32), .in_33(in_33), .out_34(out_41));

  // Other names for the same wires on the sheet: data[4:0] = in_35
endmodule

module DECODER_3x8_EN (
  input  en,
  input  a0,
  input  a1,
  input  a2,
  output y0,
  output y1,
  output y2,
  output y3,
  output y4,
  output y5,
  output y6,
  output y7
);

  wire not_1_out, not_2_out, not_3_out;

  not not_1 (not_1_out, a0);
  not not_2 (not_2_out, a1);
  not not_3 (not_3_out, a2);
  and and_1 (y0, en, not_1_out, not_2_out, not_3_out);
  and and_2 (y1, en, not_1_out, not_2_out, a2);
  and and_3 (y2, en, not_1_out, a1, not_3_out);
  and and_4 (y3, en, not_1_out, a1, a2);
  and and_5 (y4, en, a0, not_2_out, not_3_out);
  and and_6 (y5, en, a0, not_2_out, a2);
  and and_7 (y6, en, a0, a1, not_3_out);
  and and_8 (y7, en, a0, a1, a2);
endmodule

module DECODER_2x4 (
  input  s0,
  input  s1,
  output e0,
  output e1,
  output e2,
  output e3
);

  wire not_1_out, not_2_out;

  not not_1 (not_1_out, s0);
  not not_2 (not_2_out, s1);
  and and_1 (e0, not_1_out, not_2_out);
  and and_2 (e1, not_1_out, s1);
  and and_3 (e2, s0, not_2_out);
  and and_4 (e3, s0, s1);
endmodule

module MUX_32_5 (
  input  D0,
  input  D1,
  input  D2,
  input  D3,
  input  D4,
  input  D5,
  input  D6,
  input  D7,
  input  D8,
  input  D9,
  input  D10,
  input  D11,
  input  D12,
  input  [4:0] control_bit,
  input  D13,
  input  D14,
  input  D15,
  input  D16,
  input  D17,
  input  D18,
  input  D19,
  input  D20,
  input  D21,
  input  D22,
  input  D23,
  input  D24,
  input  D25,
  input  D26,
  input  D27,
  input  D28,
  input  D29,
  input  D30,
  input  D31,
  output out_34
);

  wire decoder_3x8_en_1_y0, decoder_3x8_en_1_y1, decoder_3x8_en_1_y2, decoder_3x8_en_1_y3,
       decoder_3x8_en_1_y4, decoder_3x8_en_1_y5, decoder_3x8_en_1_y6, decoder_3x8_en_1_y7,
       decoder_3x8_en_2_y0, decoder_3x8_en_2_y1, decoder_3x8_en_2_y2, decoder_3x8_en_2_y3,
       decoder_3x8_en_2_y4, decoder_3x8_en_2_y5, decoder_3x8_en_2_y6, decoder_3x8_en_2_y7,
       decoder_3x8_en_3_y0, decoder_3x8_en_3_y1, decoder_3x8_en_3_y2, decoder_3x8_en_3_y3,
       decoder_3x8_en_3_y4, decoder_3x8_en_3_y5, decoder_3x8_en_3_y6, decoder_3x8_en_3_y7,
       decoder_3x8_en_4_y0, decoder_3x8_en_4_y1, decoder_3x8_en_4_y2, decoder_3x8_en_4_y3,
       decoder_3x8_en_4_y4, decoder_3x8_en_4_y5, decoder_3x8_en_4_y6, decoder_3x8_en_4_y7, e0, e1, e2, e3;

  DECODER_2x4 decoder_2x4_1 (.s0(control_bit[3]), .s1(control_bit[4]), .e0(e0), .e1(e1), .e2(e2), .e3(e3));
  DECODER_3x8_EN decoder_3x8_en_1 (
    .en(e3), .a0(control_bit[2]), .a1(control_bit[1]), .a2(control_bit[0]), .y0(decoder_3x8_en_1_y0),
    .y1(decoder_3x8_en_1_y1), .y2(decoder_3x8_en_1_y2), .y3(decoder_3x8_en_1_y3), .y4(decoder_3x8_en_1_y4),
    .y5(decoder_3x8_en_1_y5), .y6(decoder_3x8_en_1_y6), .y7(decoder_3x8_en_1_y7));
  DECODER_3x8_EN decoder_3x8_en_2 (
    .en(e2), .a0(control_bit[2]), .a1(control_bit[1]), .a2(control_bit[0]), .y0(decoder_3x8_en_2_y0),
    .y1(decoder_3x8_en_2_y1), .y2(decoder_3x8_en_2_y2), .y3(decoder_3x8_en_2_y3), .y4(decoder_3x8_en_2_y4),
    .y5(decoder_3x8_en_2_y5), .y6(decoder_3x8_en_2_y6), .y7(decoder_3x8_en_2_y7));
  DECODER_3x8_EN decoder_3x8_en_3 (
    .en(e1), .a0(control_bit[2]), .a1(control_bit[1]), .a2(control_bit[0]), .y0(decoder_3x8_en_3_y0),
    .y1(decoder_3x8_en_3_y1), .y2(decoder_3x8_en_3_y2), .y3(decoder_3x8_en_3_y3), .y4(decoder_3x8_en_3_y4),
    .y5(decoder_3x8_en_3_y5), .y6(decoder_3x8_en_3_y6), .y7(decoder_3x8_en_3_y7));
  DECODER_3x8_EN decoder_3x8_en_4 (
    .en(e0), .a0(control_bit[2]), .a1(control_bit[1]), .a2(control_bit[0]), .y0(decoder_3x8_en_4_y0),
    .y1(decoder_3x8_en_4_y1), .y2(decoder_3x8_en_4_y2), .y3(decoder_3x8_en_4_y3), .y4(decoder_3x8_en_4_y4),
    .y5(decoder_3x8_en_4_y5), .y6(decoder_3x8_en_4_y6), .y7(decoder_3x8_en_4_y7));
  assign out_34 = decoder_3x8_en_4_y0 ? D0 : 1'bz;  // Controlled_Buffer controlled_buffer_1
  assign out_34 = decoder_3x8_en_4_y1 ? D1 : 1'bz;  // Controlled_Buffer controlled_buffer_2
  assign out_34 = decoder_3x8_en_4_y2 ? D2 : 1'bz;  // Controlled_Buffer controlled_buffer_3
  assign out_34 = decoder_3x8_en_4_y3 ? D3 : 1'bz;  // Controlled_Buffer controlled_buffer_4
  assign out_34 = decoder_3x8_en_4_y4 ? D4 : 1'bz;  // Controlled_Buffer controlled_buffer_5
  assign out_34 = decoder_3x8_en_4_y5 ? D5 : 1'bz;  // Controlled_Buffer controlled_buffer_6
  assign out_34 = decoder_3x8_en_4_y6 ? D6 : 1'bz;  // Controlled_Buffer controlled_buffer_7
  assign out_34 = decoder_3x8_en_4_y7 ? D7 : 1'bz;  // Controlled_Buffer controlled_buffer_8
  assign out_34 = decoder_3x8_en_2_y0 ? D8 : 1'bz;  // Controlled_Buffer controlled_buffer_9
  assign out_34 = decoder_3x8_en_2_y1 ? D9 : 1'bz;  // Controlled_Buffer controlled_buffer_10
  assign out_34 = decoder_3x8_en_2_y2 ? D10 : 1'bz;  // Controlled_Buffer controlled_buffer_11
  assign out_34 = decoder_3x8_en_2_y3 ? D11 : 1'bz;  // Controlled_Buffer controlled_buffer_12
  assign out_34 = decoder_3x8_en_2_y4 ? D12 : 1'bz;  // Controlled_Buffer controlled_buffer_13
  assign out_34 = decoder_3x8_en_2_y5 ? D13 : 1'bz;  // Controlled_Buffer controlled_buffer_14
  assign out_34 = decoder_3x8_en_2_y6 ? D14 : 1'bz;  // Controlled_Buffer controlled_buffer_15
  assign out_34 = decoder_3x8_en_2_y7 ? D15 : 1'bz;  // Controlled_Buffer controlled_buffer_16
  assign out_34 = decoder_3x8_en_3_y0 ? D16 : 1'bz;  // Controlled_Buffer controlled_buffer_17
  assign out_34 = decoder_3x8_en_3_y1 ? D17 : 1'bz;  // Controlled_Buffer controlled_buffer_18
  assign out_34 = decoder_3x8_en_3_y2 ? D18 : 1'bz;  // Controlled_Buffer controlled_buffer_19
  assign out_34 = decoder_3x8_en_3_y3 ? D19 : 1'bz;  // Controlled_Buffer controlled_buffer_20
  assign out_34 = decoder_3x8_en_3_y4 ? D20 : 1'bz;  // Controlled_Buffer controlled_buffer_21
  assign out_34 = decoder_3x8_en_3_y5 ? D21 : 1'bz;  // Controlled_Buffer controlled_buffer_22
  assign out_34 = decoder_3x8_en_3_y6 ? D22 : 1'bz;  // Controlled_Buffer controlled_buffer_23
  assign out_34 = decoder_3x8_en_3_y7 ? D23 : 1'bz;  // Controlled_Buffer controlled_buffer_24
  assign out_34 = decoder_3x8_en_1_y0 ? D24 : 1'bz;  // Controlled_Buffer controlled_buffer_25
  assign out_34 = decoder_3x8_en_1_y1 ? D25 : 1'bz;  // Controlled_Buffer controlled_buffer_26
  assign out_34 = decoder_3x8_en_1_y2 ? D26 : 1'bz;  // Controlled_Buffer controlled_buffer_27
  assign out_34 = decoder_3x8_en_1_y3 ? D27 : 1'bz;  // Controlled_Buffer controlled_buffer_28
  assign out_34 = decoder_3x8_en_1_y4 ? D28 : 1'bz;  // Controlled_Buffer controlled_buffer_29
  assign out_34 = decoder_3x8_en_1_y5 ? D29 : 1'bz;  // Controlled_Buffer controlled_buffer_30
  assign out_34 = decoder_3x8_en_1_y6 ? D30 : 1'bz;  // Controlled_Buffer controlled_buffer_31
  assign out_34 = decoder_3x8_en_1_y7 ? D31 : 1'bz;  // Controlled_Buffer controlled_buffer_32

  // Other names for the same wires on the sheet: d0_t = control_bit[0]; d1_t = control_bit[1]; d2_t = control_bit[2]
endmodule

module MUX_32_5_Gate (
  input  D0,
  input  D1,
  input  D2,
  input  D3,
  input  D4,
  input  D5,
  input  D6,
  input  D7,
  input  D8,
  input  D9,
  input  D10,
  input  D11,
  input  D12,
  input  [4:0] control_bit,
  input  D13,
  input  D14,
  input  D15,
  input  D16,
  input  D17,
  input  D18,
  input  D19,
  input  D20,
  input  D21,
  input  D22,
  input  D23,
  input  D24,
  input  D25,
  input  D26,
  input  D27,
  input  D28,
  input  D29,
  input  D30,
  input  D31,
  output out_34
);

  wire and_1_out, and_2_out, and_3_out, and_4_out, and_5_out, and_6_out, and_7_out, and_8_out, and_9_out,
       and_10_out, and_11_out, and_12_out, and_13_out, and_14_out, and_15_out, and_16_out, and_17_out,
       and_18_out, and_19_out, and_20_out, and_21_out, and_22_out, and_23_out, and_24_out, and_25_out,
       and_26_out, and_27_out, and_28_out, and_29_out, and_30_out, and_31_out, and_32_out,
       decoder_3x8_en_1_y0, decoder_3x8_en_1_y1, decoder_3x8_en_1_y2, decoder_3x8_en_1_y3,
       decoder_3x8_en_1_y4, decoder_3x8_en_1_y5, decoder_3x8_en_1_y6, decoder_3x8_en_1_y7,
       decoder_3x8_en_2_y0, decoder_3x8_en_2_y1, decoder_3x8_en_2_y2, decoder_3x8_en_2_y3,
       decoder_3x8_en_2_y4, decoder_3x8_en_2_y5, decoder_3x8_en_2_y6, decoder_3x8_en_2_y7,
       decoder_3x8_en_3_y0, decoder_3x8_en_3_y1, decoder_3x8_en_3_y2, decoder_3x8_en_3_y3,
       decoder_3x8_en_3_y4, decoder_3x8_en_3_y5, decoder_3x8_en_3_y6, decoder_3x8_en_3_y7,
       decoder_3x8_en_4_y0, decoder_3x8_en_4_y1, decoder_3x8_en_4_y2, decoder_3x8_en_4_y3,
       decoder_3x8_en_4_y4, decoder_3x8_en_4_y5, decoder_3x8_en_4_y6, decoder_3x8_en_4_y7, e0, e1, e2, e3,
       or_1_out, or_2_out, or_3_out, or_4_out;

  DECODER_2x4 decoder_2x4_1 (.s0(control_bit[3]), .s1(control_bit[4]), .e0(e0), .e1(e1), .e2(e2), .e3(e3));
  DECODER_3x8_EN decoder_3x8_en_1 (
    .en(e3), .a0(control_bit[2]), .a1(control_bit[1]), .a2(control_bit[0]), .y0(decoder_3x8_en_1_y0),
    .y1(decoder_3x8_en_1_y1), .y2(decoder_3x8_en_1_y2), .y3(decoder_3x8_en_1_y3), .y4(decoder_3x8_en_1_y4),
    .y5(decoder_3x8_en_1_y5), .y6(decoder_3x8_en_1_y6), .y7(decoder_3x8_en_1_y7));
  DECODER_3x8_EN decoder_3x8_en_2 (
    .en(e2), .a0(control_bit[2]), .a1(control_bit[1]), .a2(control_bit[0]), .y0(decoder_3x8_en_2_y0),
    .y1(decoder_3x8_en_2_y1), .y2(decoder_3x8_en_2_y2), .y3(decoder_3x8_en_2_y3), .y4(decoder_3x8_en_2_y4),
    .y5(decoder_3x8_en_2_y5), .y6(decoder_3x8_en_2_y6), .y7(decoder_3x8_en_2_y7));
  DECODER_3x8_EN decoder_3x8_en_3 (
    .en(e1), .a0(control_bit[2]), .a1(control_bit[1]), .a2(control_bit[0]), .y0(decoder_3x8_en_3_y0),
    .y1(decoder_3x8_en_3_y1), .y2(decoder_3x8_en_3_y2), .y3(decoder_3x8_en_3_y3), .y4(decoder_3x8_en_3_y4),
    .y5(decoder_3x8_en_3_y5), .y6(decoder_3x8_en_3_y6), .y7(decoder_3x8_en_3_y7));
  DECODER_3x8_EN decoder_3x8_en_4 (
    .en(e0), .a0(control_bit[2]), .a1(control_bit[1]), .a2(control_bit[0]), .y0(decoder_3x8_en_4_y0),
    .y1(decoder_3x8_en_4_y1), .y2(decoder_3x8_en_4_y2), .y3(decoder_3x8_en_4_y3), .y4(decoder_3x8_en_4_y4),
    .y5(decoder_3x8_en_4_y5), .y6(decoder_3x8_en_4_y6), .y7(decoder_3x8_en_4_y7));
  and and_1 (and_1_out, D0, decoder_3x8_en_4_y0);
  and and_2 (and_2_out, D1, decoder_3x8_en_4_y1);
  and and_3 (and_3_out, D2, decoder_3x8_en_4_y2);
  and and_4 (and_4_out, D3, decoder_3x8_en_4_y3);
  and and_5 (and_5_out, D4, decoder_3x8_en_4_y4);
  and and_6 (and_6_out, D5, decoder_3x8_en_4_y5);
  and and_7 (and_7_out, D6, decoder_3x8_en_4_y6);
  and and_8 (and_8_out, D7, decoder_3x8_en_4_y7);
  and and_9 (and_9_out, D8, decoder_3x8_en_2_y0);
  and and_10 (and_10_out, D9, decoder_3x8_en_2_y1);
  and and_11 (and_11_out, D10, decoder_3x8_en_2_y2);
  and and_12 (and_12_out, D11, decoder_3x8_en_2_y3);
  and and_13 (and_13_out, D12, decoder_3x8_en_2_y4);
  and and_14 (and_14_out, D13, decoder_3x8_en_2_y5);
  and and_15 (and_15_out, D14, decoder_3x8_en_2_y6);
  and and_16 (and_16_out, D15, decoder_3x8_en_2_y7);
  and and_17 (and_17_out, D16, decoder_3x8_en_3_y0);
  and and_18 (and_18_out, D17, decoder_3x8_en_3_y1);
  and and_19 (and_19_out, D18, decoder_3x8_en_3_y2);
  and and_20 (and_20_out, D19, decoder_3x8_en_3_y3);
  and and_21 (and_21_out, D20, decoder_3x8_en_3_y4);
  and and_22 (and_22_out, D21, decoder_3x8_en_3_y5);
  and and_23 (and_23_out, D22, decoder_3x8_en_3_y6);
  and and_24 (and_24_out, D23, decoder_3x8_en_3_y7);
  and and_25 (and_25_out, D24, decoder_3x8_en_1_y0);
  and and_26 (and_26_out, D25, decoder_3x8_en_1_y1);
  and and_27 (and_27_out, D26, decoder_3x8_en_1_y2);
  and and_28 (and_28_out, D27, decoder_3x8_en_1_y3);
  and and_29 (and_29_out, D28, decoder_3x8_en_1_y4);
  and and_30 (and_30_out, D29, decoder_3x8_en_1_y5);
  and and_31 (and_31_out, D30, decoder_3x8_en_1_y6);
  and and_32 (and_32_out, D31, decoder_3x8_en_1_y7);
  or or_1 (or_1_out, and_1_out, and_2_out, and_3_out, and_4_out, and_5_out, and_6_out, and_7_out, and_8_out);
  or or_2 (or_2_out, and_9_out, and_10_out, and_11_out, and_12_out, and_13_out, and_14_out, and_15_out, and_16_out);
  or or_3 (or_3_out, and_17_out, and_18_out, and_19_out, and_20_out, and_21_out, and_22_out, and_23_out, and_24_out);
  or or_4 (or_4_out, and_25_out, and_26_out, and_27_out, and_28_out, and_29_out, and_30_out, and_31_out, and_32_out);
  or or_5 (out_34, or_1_out, or_2_out, or_3_out, or_4_out);

  // Other names for the same wires on the sheet: d0_t = control_bit[0]; d1_t = control_bit[1]; d2_t = control_bit[2]
endmodule

module MUX_32_8_BIT (
  input  [4:0] ADDR,
  input  [7:0] in_2,
  input  [7:0] in_3,
  input  [7:0] in_4,
  input  [7:0] in_5,
  input  [7:0] in_6,
  input  [7:0] in_7,
  input  [7:0] in_8,
  input  [7:0] in_9,
  input  [7:0] in_10,
  input  [7:0] in_11,
  input  [7:0] in_12,
  input  [7:0] in_13,
  input  [7:0] in_14,
  input  [7:0] in_15,
  input  [7:0] in_16,
  input  [7:0] in_17,
  input  [7:0] in_18,
  input  [7:0] in_19,
  input  [7:0] in_20,
  input  [7:0] in_21,
  input  [7:0] in_22,
  input  [7:0] in_23,
  input  [7:0] in_24,
  input  [7:0] in_25,
  input  [7:0] in_26,
  input  [7:0] in_27,
  input  [7:0] in_28,
  input  [7:0] in_29,
  input  [7:0] in_30,
  input  [7:0] in_31,
  input  [7:0] in_32,
  input  [7:0] in_33,
  output [7:0] out_34
);

  MUX_32_5 mux_32_5_1 (
    .D0(in_2[1]), .D1(in_3[1]), .D2(in_4[1]), .D3(in_5[1]), .D4(in_6[1]), .D5(in_7[1]), .D6(in_8[1]),
    .D7(in_9[1]), .D8(in_10[1]), .D9(in_11[1]), .D10(in_12[1]), .D11(in_13[1]), .D12(in_14[1]),
    .control_bit(ADDR), .D13(in_15[1]), .D14(in_16[1]), .D15(in_17[1]), .D16(in_18[1]), .D17(in_19[1]),
    .D18(in_20[1]), .D19(in_21[1]), .D20(in_22[1]), .D21(in_23[1]), .D22(in_24[1]), .D23(in_25[1]),
    .D24(in_26[1]), .D25(in_27[1]), .D26(in_28[1]), .D27(in_29[1]), .D28(in_30[1]), .D29(in_31[1]),
    .D30(in_32[1]), .D31(in_33[1]), .out_34(out_34[1]));
  MUX_32_5 mux_32_5_2 (
    .D0(in_2[2]), .D1(in_3[2]), .D2(in_4[2]), .D3(in_5[2]), .D4(in_6[2]), .D5(in_7[2]), .D6(in_8[2]),
    .D7(in_9[2]), .D8(in_10[2]), .D9(in_11[2]), .D10(in_12[2]), .D11(in_13[2]), .D12(in_14[2]),
    .control_bit(ADDR), .D13(in_15[2]), .D14(in_16[2]), .D15(in_17[2]), .D16(in_18[2]), .D17(in_19[2]),
    .D18(in_20[2]), .D19(in_21[2]), .D20(in_22[2]), .D21(in_23[2]), .D22(in_24[2]), .D23(in_25[2]),
    .D24(in_26[2]), .D25(in_27[2]), .D26(in_28[2]), .D27(in_29[2]), .D28(in_30[2]), .D29(in_31[2]),
    .D30(in_32[2]), .D31(in_33[2]), .out_34(out_34[2]));
  MUX_32_5 mux_32_5_3 (
    .D0(in_2[3]), .D1(in_3[3]), .D2(in_4[3]), .D3(in_5[3]), .D4(in_6[3]), .D5(in_7[3]), .D6(in_8[3]),
    .D7(in_10[3]), .D8(in_9[3]), .D9(in_11[3]), .D10(in_12[3]), .D11(in_13[3]), .D12(in_14[3]),
    .control_bit(ADDR), .D13(in_15[3]), .D14(in_16[3]), .D15(in_17[3]), .D16(in_18[3]), .D17(in_19[3]),
    .D18(in_20[3]), .D19(in_21[3]), .D20(in_22[3]), .D21(in_23[3]), .D22(in_24[3]), .D23(in_25[3]),
    .D24(in_26[3]), .D25(in_27[3]), .D26(in_28[3]), .D27(in_29[3]), .D28(in_30[3]), .D29(in_31[3]),
    .D30(in_32[3]), .D31(in_33[3]), .out_34(out_34[3]));
  MUX_32_5 mux_32_5_4 (
    .D0(in_2[4]), .D1(in_3[4]), .D2(in_4[4]), .D3(in_5[4]), .D4(in_6[4]), .D5(in_7[4]), .D6(in_8[4]),
    .D7(in_9[4]), .D8(in_10[4]), .D9(in_11[4]), .D10(in_12[4]), .D11(in_13[4]), .D12(in_14[4]),
    .control_bit(ADDR), .D13(in_15[4]), .D14(in_16[4]), .D15(in_17[4]), .D16(in_18[4]), .D17(in_19[4]),
    .D18(in_20[4]), .D19(in_21[4]), .D20(in_22[4]), .D21(in_23[4]), .D22(in_24[4]), .D23(in_25[4]),
    .D24(in_26[4]), .D25(in_27[4]), .D26(in_28[4]), .D27(in_29[4]), .D28(in_30[4]), .D29(in_31[4]),
    .D30(in_32[4]), .D31(in_33[4]), .out_34(out_34[4]));
  MUX_32_5 mux_32_5_5 (
    .D0(in_2[5]), .D1(in_3[5]), .D2(in_4[5]), .D3(in_5[5]), .D4(in_6[5]), .D5(in_7[5]), .D6(in_8[5]),
    .D7(in_9[5]), .D8(in_10[5]), .D9(in_11[5]), .D10(in_12[5]), .D11(in_13[5]), .D12(in_14[5]),
    .control_bit(ADDR), .D13(in_15[5]), .D14(in_16[5]), .D15(in_17[5]), .D16(in_18[5]), .D17(in_19[5]),
    .D18(in_20[5]), .D19(in_21[5]), .D20(in_22[5]), .D21(in_23[5]), .D22(in_24[5]), .D23(in_25[5]),
    .D24(in_26[5]), .D25(in_27[5]), .D26(in_28[5]), .D27(in_29[5]), .D28(in_30[5]), .D29(in_31[5]),
    .D30(in_32[5]), .D31(in_33[5]), .out_34(out_34[5]));
  MUX_32_5 mux_32_5_6 (
    .D0(in_2[6]), .D1(in_3[6]), .D2(in_4[6]), .D3(in_5[6]), .D4(in_6[6]), .D5(in_7[6]), .D6(in_8[6]),
    .D7(in_9[6]), .D8(in_10[6]), .D9(in_11[6]), .D10(in_12[6]), .D11(in_13[6]), .D12(in_14[6]),
    .control_bit(ADDR), .D13(in_15[6]), .D14(in_16[6]), .D15(in_17[6]), .D16(in_18[6]), .D17(in_19[6]),
    .D18(in_20[6]), .D19(in_21[6]), .D20(in_22[6]), .D21(in_23[6]), .D22(in_24[6]), .D23(in_25[6]),
    .D24(in_26[6]), .D25(in_27[6]), .D26(in_28[6]), .D27(in_29[6]), .D28(in_30[6]), .D29(in_31[6]),
    .D30(in_32[6]), .D31(in_33[6]), .out_34(out_34[6]));
  MUX_32_5 mux_32_5_7 (
    .D0(in_2[7]), .D1(in_3[7]), .D2(in_4[7]), .D3(in_5[7]), .D4(in_6[7]), .D5(in_7[7]), .D6(in_8[7]),
    .D7(in_9[7]), .D8(in_10[7]), .D9(in_11[7]), .D10(in_12[7]), .D11(in_13[7]), .D12(in_14[7]),
    .control_bit(ADDR), .D13(in_15[7]), .D14(in_16[7]), .D15(in_17[7]), .D16(in_18[7]), .D17(in_19[7]),
    .D18(in_20[7]), .D19(in_21[7]), .D20(in_22[7]), .D21(in_23[7]), .D22(in_24[7]), .D23(in_25[7]),
    .D24(in_26[7]), .D25(in_27[7]), .D26(in_28[7]), .D27(in_29[7]), .D28(in_30[7]), .D29(in_31[7]),
    .D30(in_32[7]), .D31(in_33[7]), .out_34(out_34[7]));
  MUX_32_5 mux_32_5_8 (
    .D0(in_2[0]), .D1(in_3[0]), .D2(in_4[0]), .D3(in_5[0]), .D4(in_6[0]), .D5(in_7[0]), .D6(in_8[0]),
    .D7(in_9[0]), .D8(in_10[0]), .D9(in_11[0]), .D10(in_12[0]), .D11(in_13[0]), .D12(in_14[0]),
    .control_bit(ADDR), .D13(in_15[0]), .D14(in_16[0]), .D15(in_17[0]), .D16(in_18[0]), .D17(in_19[0]),
    .D18(in_20[0]), .D19(in_21[0]), .D20(in_22[0]), .D21(in_23[0]), .D22(in_24[0]), .D23(in_25[0]),
    .D24(in_26[0]), .D25(in_27[0]), .D26(in_28[0]), .D27(in_29[0]), .D28(in_30[0]), .D29(in_31[0]),
    .D30(in_32[0]), .D31(in_33[0]), .out_34(out_34[0]));
endmodule

module DECODER_4x16 (
  input  en,
  input  en0,
  input  en1,
  input  en2,
  input  en3,
  output y0,
  output y1,
  output y2,
  output y3,
  output y4,
  output y5,
  output y6,
  output y7,
  output y8,
  output y9,
  output y10,
  output y11,
  output y12,
  output y13,
  output y14,
  output y15
);

  wire not_1_out, not_2_out, not_3_out, not_4_out;

  not not_1 (not_1_out, en0);
  not not_2 (not_2_out, en1);
  not not_3 (not_3_out, en2);
  not not_4 (not_4_out, en3);
  and and_1 (y0, en, not_1_out, not_2_out, not_3_out, not_4_out);
  and and_2 (y1, en, not_1_out, not_2_out, not_3_out, en3);
  and and_3 (y2, en, not_1_out, not_2_out, en2, not_4_out);
  and and_4 (y3, en, not_1_out, not_2_out, en2, en3);
  and and_5 (y4, en, not_1_out, en1, not_3_out, not_4_out);
  and and_6 (y5, en, not_1_out, en1, not_3_out, en3);
  and and_7 (y6, en, not_1_out, en1, en2, not_4_out);
  and and_8 (y7, en, not_1_out, en1, en2, en3);
  and and_9 (y8, en, en0, not_2_out, not_3_out, not_4_out);
  and and_10 (y9, en, en0, not_2_out, not_3_out, en3);
  and and_11 (y10, en, en0, not_2_out, en2, not_4_out);
  and and_12 (y11, en, en0, not_2_out, en2, en3);
  and and_13 (y12, en, en0, en1, not_3_out, not_4_out);
  and and_14 (y13, en, en0, en1, not_3_out, en3);
  and and_15 (y14, en, en0, en1, en2, not_4_out);
  and and_16 (y15, en, en0, en1, en2, en3);
endmodule

module DMX_1_16 (
  input  en,
  input  [3:0] ADDR,
  output OUT0,
  output OUT1,
  output OUT2,
  output OUT3,
  output OUT4,
  output OUT5,
  output OUT6,
  output OUT7,
  output OUT8,
  output OUT9,
  output OUT10,
  output OUT11,
  output OUT12,
  output OUT13,
  output OUT14,
  output OUT15
);

  DECODER_4x16 decoder_4x16_1 (
    .en(en), .en0(ADDR[3]), .en1(ADDR[2]), .en2(ADDR[1]), .en3(ADDR[0]), .y0(OUT0), .y1(OUT1), .y2(OUT2),
    .y3(OUT3), .y4(OUT4), .y5(OUT5), .y6(OUT6), .y7(OUT7), .y8(OUT8), .y9(OUT9), .y10(OUT10), .y11(OUT11),
    .y12(OUT12), .y13(OUT13), .y14(OUT14), .y15(OUT15));
endmodule

module DMX_7bit (
  input  [3:0] ADDR,
  input  [2:0] EN,
  output [2:0] out_3,
  output [2:0] out_4,
  output [2:0] out_5,
  output [2:0] out_6,
  output [2:0] out_7,
  output [2:0] out_8,
  output [2:0] out_9,
  output [2:0] out_10,
  output [2:0] out_11,
  output [2:0] out_12,
  output [2:0] out_13,
  output [2:0] out_14,
  output [2:0] out_15,
  output [2:0] out_16,
  output [2:0] out_17,
  output [2:0] out_18
);

  DMX_1_16 dmx_1_16_1 (
    .en(EN[0]), .ADDR(ADDR), .OUT0(out_3[0]), .OUT1(out_4[0]), .OUT2(out_5[0]), .OUT3(out_6[0]),
    .OUT4(out_7[0]), .OUT5(out_8[0]), .OUT6(out_9[0]), .OUT7(out_10[0]), .OUT8(out_11[0]), .OUT9(out_12[0]),
    .OUT10(out_13[0]), .OUT11(out_14[0]), .OUT12(out_15[0]), .OUT13(out_16[0]), .OUT14(out_17[0]),
    .OUT15(out_18[0]));
  DMX_1_16 dmx_1_16_2 (
    .en(EN[1]), .ADDR(ADDR), .OUT0(out_3[1]), .OUT1(out_4[1]), .OUT2(out_5[1]), .OUT3(out_6[1]),
    .OUT4(out_7[1]), .OUT5(out_8[1]), .OUT6(out_9[1]), .OUT7(out_10[1]), .OUT8(out_11[1]), .OUT9(out_12[1]),
    .OUT10(out_13[1]), .OUT11(out_14[1]), .OUT12(out_15[1]), .OUT13(out_16[1]), .OUT14(out_17[1]),
    .OUT15(out_18[1]));
  DMX_1_16 dmx_1_16_3 (
    .en(EN[2]), .ADDR(ADDR), .OUT0(out_3[2]), .OUT1(out_4[2]), .OUT2(out_5[2]), .OUT3(out_6[2]),
    .OUT4(out_7[2]), .OUT5(out_8[2]), .OUT6(out_9[2]), .OUT7(out_10[2]), .OUT8(out_11[2]), .OUT9(out_12[2]),
    .OUT10(out_13[2]), .OUT11(out_14[2]), .OUT12(out_15[2]), .OUT13(out_16[2]), .OUT14(out_17[2]),
    .OUT15(out_18[2]));
endmodule
